# Fritzing sketch ESP_Controller_Tx_v0.9.3 (saved by Fritzing 0.9.3b)

parts:
  Left_Analog_Stick = Black Joystick KY-023
  Right_Analog_Stick = Black Joystick KY-023
  +ve = LCD1602-I2C
  LED = DUO LED RG [package="5 mm [THT]"]
  U1 = ESP32-38PinWide [part_number=ESP32-38PinWide]
  Switch_R = Toggle Switch [package=THT]
  Switch_L = Toggle Switch [package=THT]
  2S_18650_Booster_Module_Charger = 2S/3S stepup boost LIPO battery charger
  18650_2S_Li-Ion = battery_holder_single_18650
  -ve = battery_holder_single_18650
  R2 = Resistor [tolerance=±5% resistance=45k package=THT]
  R1 = Resistor [tolerance=±2% resistance=100k package="0402 [SMD]"]
  Buzzer = Piezo Speaker
  8_4v_->_5_2v = LM2596 step down module
  Master_Power_Switch = Toggle Switch [package=THT]

nets:
  N1: Left_Analog_Stick.SW, U1.GPIO26
  N2: Left_Analog_Stick.VRy, U1.GPIO34
  N3: Left_Analog_Stick.VRx, U1.GPIO35
  +5V: Left_Analog_Stick.+5V, Right_Analog_Stick.+5V, LED.common_cathode, U1.3.3
  GND: Left_Analog_Stick.GND, Right_Analog_Stick.GND, +ve.GND, U1.GND, Switch_R.L2, Switch_L.L2, 2S_18650_Booster_Module_Charger.Pin_4, 2S_18650_Booster_Module_Charger.Pin_5, 18650_2S_Li-Ion.+#0, R2.Pin_0, Buzzer.pin1, 8_4v_->_5_2v.IN-, 8_4v_->_5_2v.OUT-
  N4: Right_Analog_Stick.SW, U1.GPIO27
  N5: Right_Analog_Stick.VRy, U1.GPIO32
  N6: Right_Analog_Stick.VRx, U1.GPIO33
  VCC: +ve.VCC, U1.VIN, 8_4v_->_5_2v.OUT+
  N7: +ve.SDA, U1.GPIO21
  N8: +ve.SCL, U1.GPIO22
  N9: LED.red_anode, U1.GPIO12
  N10: LED.green_anode, U1.GPIO14
  N11: U1.GPIO36, R2.Pin_1, R1.Pin_1
  N12: U1.GPIO16, Switch_L.COM
  N13: U1.GPIO17, Switch_R.COM
  N14: U1.GPIO18, Buzzer.pin2
  N15: 2S_18650_Booster_Module_Charger.Pin_1, 2S_18650_Booster_Module_Charger.Pin_2, -ve.+#1, R1.Pin_0, Master_Power_Switch.COM
  N16: 18650_2S_Li-Ion.+#1, -ve.+#0
  N17: 8_4v_->_5_2v.IN+, Master_Power_Switch.L1

custom parts:
  Black Joystick KY-023: Description: The joystick is a combination of 2 analoog potentiometer and a digital switch. Arduino GND --> Module pin - Arduino +5V --> Module pin +5V Arduino Analoog 0 --> Module VRx Arduino Analoog 1 --> Module VRy Arduino Digital --> Module SW Dimensions: 1" x 1.25"
  LCD1602-I2C: A standard character display, usually with 2x16 characters. Comes in many colors with LCM1602 IIC attached.
  ESP32-38PinWide: Generic 38-Pin ESP32 with wide format (only access to one side of pins on a breadboard) based on Stephen Lilley's HiLetgo ESP-WROOM-32 ESP32 ESP-32S Development Board.
  2S/3S stepup boost LIPO battery charger: Type-C 2/3S Mini Li-Ion Battery Charging Module with QC Fast Charging Support with Charge Indicator Lights.
  battery_holder_single_18650: single 18650 battery holder
  LM2596 step down module: LM2596 DC-DC step down power supply module 3 A.
